# Fritzing sketch pult_scheme (saved by Fritzing 0.9.10b)
breadboards: 1

parts:
  Компонент1 = Arduino Uno (Rev3)
  S1 = Pushbutton [package="[THT]"]  # not connected
  S2 = Pushbutton [package="[THT]"]
  S3 = Pushbutton [package="[THT]"]  # not connected
  S4 = Pushbutton [package="[THT]"]
  S5 = Pushbutton [package="[THT]"]
  Компонент2 = NRF24L01
  Компонент3 = Thumb Joystick
  BAT1 = BC9VPC [package=bc9vpc]
  J1 = Camdenboss CTB0158-2 [part_number=CTB0158-2 package=THT]
  S6 = Pushbutton [package="[THT]"]
  S7 = Toggle Switch [package=THT]

nets:
  N1: Компонент1.A0, Компонент3.VERT
  N2: Компонент1.A1, Компонент3.HORZ
  N3: Компонент1.D8, S6.Pin_3
  N4: Компонент1.D9_PWM, Компонент2.CE
  N5: Компонент1.D10_PWM/SS, Компонент2.CSN
  N6: Компонент1.D11_PWM/MOSI, Компонент2.MOSI
  N7: Компонент1.D12/MISO, Компонент2.MISO
  N8: Компонент1.D13/SCK, Компонент2.SCK
  GND: Компонент1.GND, Компонент2.GND, Компонент3.GND
  N9: Компонент1.D2, S2.Pin_3
  N10: Компонент1.D5_PWM, S4.Pin_3
  N11: Компонент1.D6_PWM, S5.Pin_3
  3V3: Компонент1.3V3, Компонент2.VCC
  N12: S2.Pin_1, S2.Pin_2, S4.Pin_1, S6.Pin_1
  N13: BAT1.V+, S7.L1
  N14: BAT1.V-, J1.pin2
  N15: J1.pin1, S7.COM
