# Fritzing sketch robot_scheme (saved by Fritzing 0.9.10b)
stripboards: 1

parts:
  Компонент3 = NRF24L01
  HC-SR04_Sensor_1 = HC-SR04 Ultrasonic Distance Sensor
  Mod1 = Arduino Sensor Shield v5.0
  M1 = gear-motor
  M2 = gear-motor
  Компонент4 = Arduino Motor Shield (Rev3)
  Mod2 = Arduino Sensor Shield v5.0
  S1 = Toggle Switch [package=THT]
  S2 = Toggle Switch [package=THT]
  J2 = Basic Servo
  BAT2 = Battery Holders [package=lipo-1100mAh]
  BAT3 = Battery Holders [package=lipo-1100mAh]
  BAT4 = Battery Holders [package=lipo-1100mAh]
  BAT5 = Battery Holders [package=lipo-1100mAh]
  BAT6 = Battery Holders [package=lipo-1100mAh]
  J3 = Basic Servo
  J1 = Basic Servo  # not connected

nets:
  N1: Компонент3.MOSI, Компонент3.VCC, Mod1.SD-D11, Mod1.11-S, Mod1.ParallelLCD-D11
  N2: Компонент3.CSN, Mod1.10-S, Mod1.ParallelLCD-D10
  N3: Компонент3.MISO, Mod1.12-S, Mod1.ParallelLCD-D12
  GND: Компонент3.SCK, Mod1.SD-D13, Mod1.13-S, Mod1.ParallelLCD-D13, Mod2.SD-D13, Mod2.13-S, J2.gnd, BAT5.-, BAT6.-, J3.gnd
  N4: Компонент3.CE, Mod1.9-S, Mod1.ParallelLCD-D9
  GND_2: Компонент3.GND, HC-SR04_Sensor_1.GND, Mod1.GND, Mod1.12-G, Mod1.8-G, Mod1.ParallelLCD-GND
  N5: HC-SR04_Sensor_1.VCC, Mod1.8-V, Mod1.ParallelLCD-VCC
  N6: HC-SR04_Sensor_1.TRIG, Mod1.8-S, Mod1.ParallelLCD-D8
  N7: HC-SR04_Sensor_1.ECHO, Mod1.URF01-A0, Mod1.A0-SIG
  N8: Mod1.A4-SIG, Mod2.A4-SIG, Mod2.IIC-SDA
  N9: Mod1.A5-SIG, Mod2.A5-SIG, Mod2.IIC-SCL
  N10: M1.pin_1, Компонент4.B+
  N11: M1.pin_2, Компонент4.B-
  N12: M2.pin_1, Компонент4.A+
  N13: M2.pin_2, Компонент4.A-
  N14: Компонент4.VMOT, S1.COM
  N15: Компонент4.GND, BAT2.-, BAT3.-, BAT4.-
  N16: S1.L1, BAT2.+, BAT3.+, BAT4.+
  VCC: S2.COM, J2.vcc, J3.vcc
  N17: S2.L2, BAT5.+, BAT6.+
